// Logisim project SAP_1.circ as structural Verilog
module main (
);

  InputAndMAR inputandmar_1 ();  // open: Lm, CLK, in_2, out_4, out_5
  RAM16x8 ram16x8_1 ();  // open: CE, in_1, in_2, out_4
  InstructionRegister instructionregister_1 ();  // open: Li, CLK, CLR, Ei, in_2, out_7, out_6
  Controller controller_1 ();  // open: in_1, out_6, CLK, nCLK, CLR, nCLR
  ProgramCounter programcounter_1 ();  // open: Cp, CLK, CLR, Ep, out_5
  AccumulatorA accumulatora_1 ();
  AdderSubtractor addersubtractor_1 ();
  BRegister bregister_1 ();
  OutputRegister outputregister_1 ();
  BinaryDisplay binarydisplay_1 ();
endmodule

module ProgramCounter (
  input  Cp,
  input  CLK,
  input  CLR,
  input  Ep,
  output [3:0] out_5
);
endmodule

module InputAndMAR (
  input  Lm,
  input  [3:0] in_2,
  input  CLK,
  output [3:0] out_4,
  output [3:0] out_5
);
endmodule

module RAM16x8 (
  input  [3:0] in_1,
  input  [3:0] in_2,
  input  CE,
  output [7:0] out_4
);
endmodule

module InstructionRegister (
  input  Li,
  input  [7:0] in_2,
  input  CLK,
  input  CLR,
  input  Ei,
  output [3:0] out_6,
  output [3:0] out_7
);
endmodule

module Controller (
  input  [3:0] in_1,
  output CLK,
  output nCLK,
  output CLR,
  output nCLR,
  output [11:0] out_6
);
endmodule
